# Fritzing sketch 2color-led-module (saved by Fritzing 0.9.2b)
breadboards: 1

parts:
  Raspberry_Pi1 = Raspberry Pi 2
  T1 = LM35 Temperature Sensor [package="TO92 [THT]"]
  R2 = Resistor [tolerance=±5% resistance=220 package=THT]
  R3 = Resistor [tolerance=±5% resistance=220 package=THT]

nets:
  N1: Raspberry_Pi1.GPIO15, R3.Pin_0
  N2: Raspberry_Pi1.GPIO14, R2.Pin_0
  GND: Raspberry_Pi1.GND, T1.GND
  N3: T1.+Vs, R3.Pin_1
  N4: T1.Vout, R2.Pin_1
