# Fritzing sketch ky-013-temperature-sensor (saved by Fritzing 0.9.2b)
breadboards: 1

parts:
  Raspberry_Pi1 = Raspberry Pi 2
  Q1 = PNP-Transistor [package="TO92 [THT]"]

nets:
  N1: Raspberry_Pi1.3v3, Q1.B
  N2: Raspberry_Pi1.GPIO4, Q1.C
  N3: Raspberry_Pi1.GND, Q1.E
