# Fritzing sketch temp-humidity-module (saved by Fritzing 0.9.2b)
breadboards: 1

parts:
  Raspberry_Pi1 = Raspberry Pi 2
  DHT22 = LM35 Temperature Sensor [package="TO92 [THT]"]
  R1_8_7kOhm = Resistor [tolerance=±5% resistance=220 package=THT]

nets:
  N1: Raspberry_Pi1.3v3, DHT22.Vout, R1_8_7kOhm.Pin_1
  N2: Raspberry_Pi1.GPIO14, DHT22.GND, R1_8_7kOhm.Pin_0
  N3: Raspberry_Pi1.GND, DHT22.+Vs
