# Fritzing sketch rgb-led-modul (saved by Fritzing 0.9.2b)
breadboards: 1

parts:
  Raspberry_Pi_B_rev1 = Raspberry Pi B rev1
  U1 = QRD1114 [package=qrd1114]
  R1 = Resistor [tolerance=±5% resistance=220 package=THT]
  R2 = Resistor [tolerance=±5% resistance=220 package=THT]
  R3 = Resistor [tolerance=±5% resistance=220 package=THT]

nets:
  N1: Raspberry_Pi_B_rev1.GND, U1.A
  N2: Raspberry_Pi_B_rev1.GPIO_14, R3.Pin_0
  N3: Raspberry_Pi_B_rev1.GPIO_15, R2.Pin_0
  N4: Raspberry_Pi_B_rev1.GPIO_18, R1.Pin_0
  N5: U1.E, R2.Pin_1
  N6: U1.C, R1.Pin_1
  N7: U1.K, R3.Pin_1
