# Fritzing sketch photoresistor (saved by Fritzing 0.9.2b)
breadboards: 1

parts:
  IC1 = ADS1115 16-bit ADC Breakout
  Raspberry_Pi_B_rev1 = Raspberry Pi B rev1
  T1 = LM35 Temperature Sensor [package="TO92 [THT]"]

nets:
  VDD: IC1.VDD, Raspberry_Pi_B_rev1.3V3
  GND: IC1.GND, Raspberry_Pi_B_rev1.GND, T1.GND
  N1: IC1.SCL, Raspberry_Pi_B_rev1.GPIO_1
  N2: IC1.SDA, Raspberry_Pi_B_rev1.GPIO_0
  N3: IC1.A0, T1.+Vs
  N4: Raspberry_Pi_B_rev1.5V, T1.Vout

custom parts:
  ADS1115 16-bit ADC Breakout: ADS1015 12-bit I2C ADC+PGA Breakout
