# Fritzing sketch 5volt-relais (saved by Fritzing 0.9.2b)

parts:
  Raspberry_Pi1 = Raspberry Pi 2
  U6 = G3VM-61E1 [package=g3vm-61e1]
  VCC1 = Battery block 9V  # not connected
  M1 = DC Motor  # not connected

nets:
  N1: Raspberry_Pi1.GPIO14, U6.P$4
  N2: Raspberry_Pi1.GND, U6.P$6
  N3: Raspberry_Pi1.5V, U6.P$5
