# Fritzing sketch mini-magnetic-reed-module (saved by Fritzing 0.9.2b)
breadboards: 1

parts:
  Raspberry_Pi1 = Raspberry Pi 2
  LED2 = LED - 5mm [color="Red (633nm)" package="5 mm [THT]"]
  R2 = Resistor [tolerance=±5% resistance=220 package=THT]
  T1 = LM35 Temperature Sensor [package="TO92 [THT]"]

nets:
  N1: Raspberry_Pi1.3v3, T1.Vout
  N2: Raspberry_Pi1.GPIO4, LED2.cathode
  N3: Raspberry_Pi1.GPIO14, T1.GND
  N4: Raspberry_Pi1.GND, R2.Pin_1, T1.+Vs
  N5: LED2.anode, R2.Pin_0
