# Fritzing sketch temperature-sensor (saved by Fritzing 0.9.2b)
breadboards: 1

parts:
  IC1 = ADS1115 16-bit ADC Breakout
  Raspberry_Pi_B_rev1 = Raspberry Pi B rev1
  U1 = QRD1114 [package=qrd1114]

nets:
  VDD: IC1.VDD, Raspberry_Pi_B_rev1.3V3, U1.E
  GND: IC1.GND, Raspberry_Pi_B_rev1.GND, U1.C
  N1: IC1.SCL, Raspberry_Pi_B_rev1.GPIO_1
  N2: IC1.SDA, Raspberry_Pi_B_rev1.GPIO_0
  N3: IC1.A0, U1.A
  N4: Raspberry_Pi_B_rev1.GPIO_18, U1.K

custom parts:
  ADS1115 16-bit ADC Breakout: ADS1015 12-bit I2C ADC+PGA Breakout
