# Fritzing sketch barrier-detector (saved by Fritzing 0.9.2b)
breadboards: 1

parts:
  Raspberry_Pi_B_rev1 = Raspberry Pi B rev1
  U1 = QRD1114 [package=qrd1114]

nets:
  N1: Raspberry_Pi_B_rev1.3V3, U1.C
  N2: Raspberry_Pi_B_rev1.GND, U1.A
  N3: Raspberry_Pi_B_rev1.GPIO_18, U1.E
