# Fritzing sketch rotary-encoder-module (saved by Fritzing 0.9.2b)

parts:
  Raspberry_Pi1 = Raspberry Pi 2
  U1 = POT_SWITCH [package=pot_pth_switch]

nets:
  N1: Raspberry_Pi1.3v3, U1.G$1_S
  N2: Raspberry_Pi1.GPIO18, U1.G$2_2
  N3: Raspberry_Pi1.GPIO15, U1.G$2_1
  N4: Raspberry_Pi1.GPIO14, U1.G$1_A
  N5: Raspberry_Pi1.GND, U1.G$1_E
