# Fritzing sketch air-pressure-sensor (saved by Fritzing 0.9.2b)
breadboards: 1

parts:
  Raspberry_Pi_B_rev1 = Raspberry Pi B rev1
  U1 = QRD1114 [package=qrd1114]

nets:
  N1: Raspberry_Pi_B_rev1.3V3, U1.K
  N2: Raspberry_Pi_B_rev1.GPIO_0, U1.E
  N3: Raspberry_Pi_B_rev1.GPIO_1, U1.C
  N4: Raspberry_Pi_B_rev1.GND, U1.A
