# Fritzing sketch ky-006 (saved by Fritzing 0.9.2b)
breadboards: 1

parts:
  Raspberry_Pi1 = Raspberry Pi 2
  Q1 = PNP-Transistor [package="TO92 [THT]"]

nets:
  N1: Raspberry_Pi1.GPIO18, Q1.E
  N2: Raspberry_Pi1.GND, Q1.C
