# Fritzing sketch 4-digit-7-segment (saved by Fritzing 0.9.2b)
breadboards: 1

parts:
  7_Segment1 = 7 Segment Display
  Raspberry_Pi1 = Raspberry Pi 2
  R1 = Resistor [tolerance=±5% resistance=220 package="2010 [SMD]"]
  R2 = Resistor [tolerance=±5% resistance=220 package="2010 [SMD]"]
  R3 = Resistor [tolerance=±5% resistance=220 package="2010 [SMD]"]
  R4 = Resistor [tolerance=±5% resistance=220 package="2010 [SMD]"]
  R5 = Resistor [tolerance=±5% resistance=220 package="2010 [SMD]"]
  R6 = Resistor [tolerance=±5% resistance=220 package="2010 [SMD]"]
  R7 = Resistor [tolerance=±5% resistance=220 package="2010 [SMD]"]
  R8 = Resistor [tolerance=±5% resistance=220 package="2010 [SMD]"]

nets:
  N1: 7_Segment1.Segment_G, Raspberry_Pi1.GPIO24, R7.Pin_0, R7.Pin_1
  N2: 7_Segment1.Segment_F, Raspberry_Pi1.GPIO25, R6.Pin_0, R6.Pin_1
  N3: 7_Segment1.common_anode, Raspberry_Pi1.GPIO9, Raspberry_Pi1.GPIO8, R2.Pin_0, R2.Pin_1
  N4: 7_Segment1.Segment_E, Raspberry_Pi1.GPIO7, R5.Pin_0, R5.Pin_1
  N5: 7_Segment1.Segment_D, Raspberry_Pi1.GPIO11
  N6: 7_Segment1.Segment_DP, Raspberry_Pi1.GPIO14, R1.Pin_0, R1.Pin_1
  N7: 7_Segment1.Segment_C, Raspberry_Pi1.GPIO10
  N8: 7_Segment1.Segment_B, Raspberry_Pi1.GPIO15, R4.Pin_0, R4.Pin_1
  N9: 7_Segment1.Segment_A, Raspberry_Pi1.GPIO18, R3.Pin_0, R3.Pin_1
  N10: Raspberry_Pi1.GPIO23, R8.Pin_0, R8.Pin_1
