# Fritzing sketch 7-segment-led (saved by Fritzing 0.9.2b)
breadboards: 1

parts:
  Raspberry_Pi_B_rev1 = Raspberry Pi B rev1
  U2 = 7-SEGMENT-DISPLAY [package=7-segment-display]

nets:
  N1: Raspberry_Pi_B_rev1.GND, U2.C, U2.F
  N2: Raspberry_Pi_B_rev1.GPIO_23, U2.B
  N3: Raspberry_Pi_B_rev1.GPIO_14, U2.D
  N4: Raspberry_Pi_B_rev1.GPIO_15, U2.G1
  N5: Raspberry_Pi_B_rev1.GPIO_18, U2.DP
  N6: Raspberry_Pi_B_rev1.GPIO_24, U2.A
  N7: Raspberry_Pi_B_rev1.GPIO_25, U2.G2
  N8: Raspberry_Pi_B_rev1.GPIO_8, U2.G
  N9: Raspberry_Pi_B_rev1.GPIO_7, U2.E
