# Fritzing sketch dualLED (saved by Fritzing 0.9.2b)
breadboards: 1

parts:
  Raspberry_Pi1 = Raspberry Pi 2
  LED1 = LED - 5mm [color="Red (633nm)" package="5 mm [THT]"]
  R1 = Resistor [tolerance=±5% resistance=220 package=THT]
  LED2 = LED - 5mm [color="Red (633nm)" package="5 mm [THT]"]
  R2 = Resistor [tolerance=±5% resistance=220 package=THT]

nets:
  N1: Raspberry_Pi1.GPIO17, LED1.cathode
  N2: Raspberry_Pi1.GPIO18, LED2.cathode
  N3: Raspberry_Pi1.GND, R1.Pin_1, R2.Pin_1
  N4: LED1.anode, R1.Pin_0
  N5: LED2.anode, R2.Pin_0
