# Fritzing sketch easyLED (saved by Fritzing 0.9.2b)
breadboards: 1

parts:
  Raspberry_Pi1 = Raspberry Pi 2
  LED1 = LED - 5mm [color="Red (633nm)" package="5 mm [THT]"]
  R1 = Resistor [tolerance=±5% resistance=220 package=THT]

nets:
  N1: Raspberry_Pi1.GPIO18, LED1.cathode
  N2: Raspberry_Pi1.GND, R1.Pin_1
  N3: LED1.anode, R1.Pin_0
