# Fritzing sketch project-x (saved by Fritzing 0.9.2b)
breadboards: 1

parts:
  Raspberry_Pi_B_rev1 = Raspberry Pi B rev1
  7SEG1 = 7-Segment LED I2C Backpack (green)
  BB1 = 4-Line Bi-Directional Level Shifter

nets:
  N1: Raspberry_Pi_B_rev1.3V3, BB1.LV
  N2: Raspberry_Pi_B_rev1.5V, 7SEG1.V+, BB1.HV
  N3: Raspberry_Pi_B_rev1.GPIO_0, BB1.A1
  N4: Raspberry_Pi_B_rev1.GPIO_1, BB1.A2
  GND: Raspberry_Pi_B_rev1.GND, 7SEG1.GND, BB1.GND
  N5: 7SEG1.SDA, BB1.B1
  N6: 7SEG1.SCL, BB1.B2

custom parts:
  7-Segment LED I2C Backpack (green): 4-digit, 7-segment LED Display with I2C Control
  4-Line Bi-Directional Level Shifter: 4-Channel Bi-Directional Level Shifter
