# Fritzing sketch pushButton (saved by Fritzing 0.9.2b)
breadboards: 1

parts:
  Raspberry_Pi1 = Raspberry Pi 2
  S1 = Momentary Switch [package=ksa_sealed_tac_switch]

nets:
  N1: Raspberry_Pi1.GPIO14, S1.2
  N2: Raspberry_Pi1.GND, S1.4
