# Fritzing sketch servoSg90 (saved by Fritzing 0.9.2b)
breadboards: 1

parts:
  Raspberry_Pi1 = Raspberry Pi 2
  J1 = Basic Servo

nets:
  N1: Raspberry_Pi1.GPIO14, J1.pulse
  GND: Raspberry_Pi1.GND, J1.gnd
  5V: Raspberry_Pi1.5V, J1.vcc
